# Fritzing sketch house_schema (saved by Fritzing 0.8.7b)
breadboards: 1

parts:
  Composant1 = Arduino Mega 2560 (Rev3)
  LCD1 = LCD screen
  J1 = Piezo Speaker
  LED1 = LED - 5mm [color="Red (633nm)" package="5 mm [THT]"]
  R1 = Photocell (LDR) [package=THT]
  Composant2 = Real Time Clock Module - DS1307 RTC Breakout Board
  S1 = Square Pushbutton
  S2 = Round Pushbutton
  J2 = Basic Servo
  U1 = POT [package=pot_alpha_rv16af-20]
  R2 = Resistor [tolerance=±5% resistance=220 package=THT]

nets:
  N1: Composant1.A0, R1.pin_1, R2.Pin_0
  N2: Composant1.SCL, Composant2.SCL
  N3: Composant1.SDA, Composant2.SDA
  N4: Composant1.D13_PWM, S1.leg1
  N5: Composant1.D12_PWM, J2.pulse
  N6: Composant1.D11_PWM, J1.pin2
  N7: Composant1.D10_PWM, S2.leg1
  N8: Composant1.D9_PWM, LED1.anode
  N9: Composant1.D2_PWM, LCD1.RS
  N10: Composant1.D3_PWM, LCD1.E
  N11: Composant1.D4_PWM, LCD1.DB4
  N12: Composant1.D5_PWM, LCD1.DB5
  N13: Composant1.D6_PWM, LCD1.DB6
  N14: Composant1.D7_PWM, LCD1.DB7
  GND: LCD1.VSS, LCD1.R/W, LCD1.LED-, J1.pin1, LED1.cathode, R1.pin_0, Composant2.GND, S1.leg0, S2.leg0, J2.gnd, U1.A, R2.Pin_1
  VDD: LCD1.VDD, LCD1.LED+, Composant2.5V, J2.vcc, U1.E
  N15: LCD1.V0, U1.S
